// Logisim project Logisism Problem 6.circ as structural Verilog: 1 circuit, main circuit main
module main (
  input  A,
  input  B,
  output out_3
);

  wire transistor_2_out;

  Transistor #(.\type ("n")) transistor_1 (.in(1'b0), .out(out_3), .gate(A));
  Transistor transistor_2 (.in(1'b1), .out(transistor_2_out), .gate(A));
  Transistor transistor_3 (.in(transistor_2_out), .out(out_3), .gate(B));
  Transistor #(.\type ("n")) transistor_4 (.in(1'b0), .out(out_3), .gate(B));
endmodule
