// Logisim project add1.circ as structural Verilog: 2 circuits, main circuit main
module main (
  input  [7:0] in_1,
  output [7:0] out_2,
  output Carry
);

  wire subcirc_1_scarry, subcirc_2_scarry, subcirc_3_scarry, subcirc_4_scarry, subcirc_5_scarry,
       subcirc_6_scarry, subcirc_7_scarry;

  subCirc subcirc_1 (.in_1(in_1[0]), .in_2(1'b1), .Sum(out_2[0]), .Scarry(subcirc_1_scarry));
  subCirc subcirc_2 (.in_1(in_1[1]), .in_2(subcirc_1_scarry), .Sum(out_2[1]), .Scarry(subcirc_2_scarry));
  subCirc subcirc_3 (.in_1(in_1[2]), .in_2(subcirc_2_scarry), .Sum(out_2[2]), .Scarry(subcirc_3_scarry));
  subCirc subcirc_4 (.in_1(in_1[3]), .in_2(subcirc_3_scarry), .Sum(out_2[3]), .Scarry(subcirc_4_scarry));
  subCirc subcirc_5 (.in_1(in_1[4]), .in_2(subcirc_4_scarry), .Sum(out_2[4]), .Scarry(subcirc_5_scarry));
  subCirc subcirc_6 (.in_1(in_1[5]), .in_2(subcirc_5_scarry), .Sum(out_2[5]), .Scarry(subcirc_6_scarry));
  subCirc subcirc_7 (.in_1(in_1[6]), .in_2(subcirc_6_scarry), .Sum(out_2[6]), .Scarry(subcirc_7_scarry));
  subCirc subcirc_8 (.in_1(in_1[7]), .in_2(subcirc_7_scarry), .Sum(out_2[7]), .Scarry(Carry));
endmodule

module subCirc (
  input  in_1,
  input  in_2,
  output Sum,
  output Scarry
);

  wire _01_out, _10_out;

  // AND_Gate _00 has open pins: in0=in_1, in2=in_2, out=open
  and _01 (_01_out, ~in_1, in_2);  // AND_Gate
  and _10 (_10_out, in_1, ~in_2);  // AND_Gate
  and _11 (Scarry, in_1, in_2);
  or or_1 (Sum, _01_out, _10_out);
endmodule
