// Logisim project R12.circ as structural Verilog: 1 circuit, main circuit main
module main (
  input  I,
  output O
);

  wire _01_out, _10_out, _11_out, or_1_out, T, T2;

  and _01 (_01_out, ~T2, I);  // AND_Gate
  and _10 (_10_out, T2, ~I);  // AND_Gate
  and _11 (_11_out, T2, I);
  or or_1 (or_1_out, _01_out, _11_out);
  D_Flip_Flop d_ff_1 (.clk(T), .D(_10_out), .Q(O));  // open: Qn, preset, en, reset
  Clock clock_1 (.out(T));
  D_Flip_Flop State (.clk(T), .D(or_1_out), .Q(T2));  // open: Qn, preset, en, reset

  // Notes on the sheet:
  //   D = Next State
  //   Q = Current State
endmodule
